// Logisim project tab_dec_iso.circ as structural Verilog: 1 circuit, main circuit main
module main (
  input  in2,
  input  d_in1,
  input  in1,
  input  d_in0,
  input  in0,
  output out3,
  output t_out1,
  output out2,
  output out1,
  output out0,
  output t_out0
);

  wire and_1_out, and_2_out, and_3_out, and_4_out, and_5_out, and_6_out, and_7_out;

  and and_1 (and_1_out, in2, in0);
  and and_2 (and_2_out, in1, in0);
  and and_3 (and_3_out, in2, in1);
  and and_4 (and_4_out, ~in2, ~in1, in0);  // AND_Gate
  and and_5 (and_5_out, ~in2, in1, ~in0);  // AND_Gate
  and and_6 (and_6_out, in2, ~in1, ~in0);  // AND_Gate
  and and_7 (and_7_out, in2, in1, in0);
  or or_1 (t_out1, and_1_out, and_2_out, and_3_out);
  or or_2 (t_out0, and_4_out, and_5_out, and_6_out, and_7_out);
  and and_8 (out3, d_in1, d_in0);
  and and_9 (out2, d_in1, ~d_in0);  // AND_Gate
  and and_10 (out1, ~d_in1, d_in0);  // AND_Gate
  and and_11 (out0, ~d_in1, ~d_in0);  // AND_Gate
endmodule
