// Logisim project add1_schem.circ as structural Verilog
module add1 (
  input  a,
  input  b,
  input  cin,
  output sum,
  output cout
);

  wire and_1_out, and_2_out, and_3_out, and_4_out, and_5_out, and_6_out, and_7_out, not_1_out, not_2_out,
       not_3_out;

  not not_1 (not_1_out, a);
  not not_2 (not_2_out, b);
  not not_3 (not_3_out, cin);
  and and_1 (and_1_out, not_1_out, not_2_out, cin);
  and and_2 (and_2_out, not_1_out, b, not_3_out);
  and and_3 (and_3_out, a, not_2_out, not_3_out);
  and and_4 (and_4_out, a, b, cin);
  and and_5 (and_5_out, b, cin);
  and and_6 (and_6_out, a, cin);
  and and_7 (and_7_out, a, b);
  or or_1 (sum, and_1_out, and_2_out, and_3_out, and_4_out);
  or or_2 (cout, and_5_out, and_6_out, and_7_out);
endmodule
