// Logisim project addsub3.circ as structural Verilog: 5 circuits, main circuit ripple_add3_ovf
module ripple_add3_ovf (
  input  cin,
  input  [2:0] a,
  input  [2:0] b,
  output [2:0] s,
  output ovf
);

  wire add1_1_cout, add1_2_cout, add1_3_cout;

  add1 add1_1 (.a(a[0]), .b(b[0]), .cin(cin), .sum(s[0]), .cout(add1_1_cout));
  add1 add1_2 (.a(a[1]), .b(b[1]), .cin(add1_1_cout), .sum(s[1]), .cout(add1_2_cout));
  add1 add1_3 (.a(a[2]), .b(b[2]), .cin(add1_2_cout), .sum(s[2]), .cout(add1_3_cout));
  xor xor_1 (ovf, add1_3_cout, add1_2_cout);
endmodule

module mux2x1 (
  input  in1,
  input  s,
  input  in0,
  output out0
);

  wire and_1_out, and_2_out;

  and and_1 (and_1_out, in1, s);
  and and_2 (and_2_out, ~s, in0);  // AND_Gate
  or or_1 (out0, and_1_out, and_2_out);
endmodule

module mux2x1_3b (
  input  [2:0] in0,
  input  [2:0] in1,
  input  s,
  output [2:0] out0
);

  mux2x1 mux2x1_1 (.in1(in1[0]), .s(s), .in0(in0[0]), .out0(out0[0]));
  mux2x1 mux2x1_2 (.in1(in1[1]), .s(s), .in0(in0[1]), .out0(out0[1]));
  mux2x1 mux2x1_3 (.in1(in1[2]), .s(s), .in0(in0[2]), .out0(out0[2]));
endmodule

module add1 (
  input  a,
  input  b,
  input  cin,
  output sum,
  output cout
);

  wire and_1_out, and_2_out, and_3_out, and_4_out, and_5_out, and_6_out, and_7_out, not_1_out, not_2_out,
       not_3_out;

  not not_1 (not_1_out, a);
  not not_2 (not_2_out, b);
  not not_3 (not_3_out, cin);
  and and_1 (and_1_out, not_1_out, not_2_out, cin);
  and and_2 (and_2_out, not_1_out, b, not_3_out);
  and and_3 (and_3_out, a, not_2_out, not_3_out);
  and and_4 (and_4_out, a, b, cin);
  and and_5 (and_5_out, b, cin);
  and and_6 (and_6_out, a, cin);
  and and_7 (and_7_out, a, b);
  or or_1 (sum, and_1_out, and_2_out, and_3_out, and_4_out);
  or or_2 (cout, and_5_out, and_6_out, and_7_out);
endmodule

module addsub3 (
  input  [2:0] a,
  input  [2:0] b,
  input  sub,
  output [2:0] f,
  output ovf
);

  wire [2:0] mux2x1_3b_1_out0, not_1_out;

  assign not_1_out = ~b;  // NOT_Gate not_1, 3 bits wide
  mux2x1_3b mux2x1_3b_1 (.in0(b), .in1(not_1_out), .s(sub), .out0(mux2x1_3b_1_out0));
  ripple_add3_ovf ripple_add3_ovf_1 (.cin(sub), .a(a), .b(mux2x1_3b_1_out0), .s(f), .ovf(ovf));
endmodule
