// Logisim project mux2x1_3b.circ as structural Verilog: 1 circuit, main circuit main
module main (
  input  [2:0] in0,
  input  [2:0] in1,
  input  s,
  output [2:0] out0
);

  mux2x1 mux2x1_1 (.in1(in1[0]), .s(s), .in0(in0[0]), .out0(out0[0]));
  mux2x1 mux2x1_2 (.in1(in1[1]), .s(s), .in0(in0[1]), .out0(out0[1]));
  mux2x1 mux2x1_3 (.in1(in1[2]), .s(s), .in0(in0[2]), .out0(out0[2]));
endmodule
