// Logisim project mux2x1_lib.circ as structural Verilog: 1 circuit, main circuit mux2x1
module mux2x1 (
  input  in1,
  input  s,
  input  in0,
  output out0
);

  wire and_1_out, and_2_out;

  and and_1 (and_1_out, in1, s);
  and and_2 (and_2_out, ~s, in0);  // AND_Gate
  or or_1 (out0, and_1_out, and_2_out);
endmodule
