// Logisim project calculator.circ as structural Verilog: 3 circuits, main circuit calculator
module calculator (
  output [3:0] a,
  output [3:0] f,
  output [3:0] alu_op,
  output [3:0] b
);

  wire clk_out;

  Clock clk (.out(clk_out));
  DipSwitch #(.number(4)) dipswitch_1 (.sw1(alu_op[3]), .sw2(alu_op[2]), .sw3(alu_op[1]), .sw4(alu_op[0]));
  DipSwitch #(.number(4)) dipswitch_2 (.sw1(b[3]), .sw2(b[2]), .sw3(b[1]), .sw4(b[0]));
  reg4 reg4_1 (.d(f), .clk(clk_out), .q(a));
  Hex_Digit_Display HEX3 (.value(a));  // open: dp
  Hex_Digit_Display HEX0 (.value(f));  // open: dp
  alu alu_1 (.a(a), .b(b), .alu_op(alu_op), .f(f));
  Hex_Digit_Display HEX1 (.value(alu_op));  // open: dp
  Hex_Digit_Display HEX2 (.value(b));  // open: dp

  // Notes on the sheet:
  //   alu_op[3:0]
  //   b[3:0]
  //   a[3:0]
  //   f[3:0]
  //   alu_op[3:0]
  //   b[3:0]
endmodule

module alu (
  input  [3:0] a,
  input  [3:0] b,
  input  [3:0] alu_op,
  output [3:0] f
);

  wire or_2_out;
  wire [3:0] adder_1_out, and_1_out, multiplexer_1_out, multiplexer_2_out, multiplier_1_out, not_1_out,
       or_1_out, shifter_1_out, shifter_2_out, subtractor_1_out, xor_1_out;

  Adder #(.width(4)) adder_1 (.a(a), .b(b), .out(adder_1_out));  // open: cin, cout
  Subtractor #(.width(4)) subtractor_1 (.a(a), .b(b), .out(subtractor_1_out));  // open: bin, bout
  assign and_1_out = a & b;  // AND_Gate and_1, 4 bits wide
  assign or_1_out = a | b;  // OR_Gate or_1, 4 bits wide
  Shifter #(.width(4)) shifter_1 (.in(a), .\dist (b[1:0]), .out(shifter_1_out));
  or or_2 (or_2_out, b[2], b[3]);
  Shifter #(.shift("lr"), .width(4)) shifter_2 (.in(a), .\dist (b[1:0]), .out(shifter_2_out));
  assign xor_1_out = a ^ b;  // XOR_Gate xor_1, 4 bits wide
  Multiplier #(.mode("twosComplement"), .width(4)) multiplier_1 (
    .a(a), .b(b), .out(multiplier_1_out));  // open: cin, cout
  assign not_1_out = ~a;  // NOT_Gate not_1, 4 bits wide
  Multiplexer #(.width(4)) multiplexer_1 (.in0(shifter_1_out), .in1(4'b0000), .out(multiplexer_1_out), .sel(or_2_out));
  Multiplexer #(.width(4)) multiplexer_2 (.in0(shifter_2_out), .in1(4'b0000), .out(multiplexer_2_out), .sel(or_2_out));
  Multiplexer #(.select(4), .width(4)) multiplexer_3 (
    .in0(adder_1_out), .in1(subtractor_1_out), .in2(and_1_out), .in3(or_1_out), .in4(not_1_out),
    .in5(multiplexer_1_out), .in6(multiplexer_2_out), .in7(b), .in8(xor_1_out), .in9(multiplier_1_out),
    .out(f), .sel(alu_op));  // open: in10, in11, in12, in13, in14, in15
endmodule

module reg4 (
  input  [3:0] d,
  input  clk,
  output [3:0] q
);

  Register #(.width(4)) register_1 (.D(d), .en(1'b1), .clk(clk), .Q(q), .clr(1'b0));
endmodule
