// Logisim project hardware_divider.circ as structural Verilog: 6 circuits, main circuit load_register8
module load_register8 (
  input  [7:0] d,
  input  en,
  input  clk,
  input  rst,
  output [7:0] q
);

  Register register_1 (.D(d), .en(en), .clk(clk), .Q(q), .clr(rst));
endmodule

module div_datapath (
  input  clk,
  input  en_quotient,
  input  [1:0] sel_quotient,
  input  en_i,
  input  sel_i,
  input  [3:0] dividend_in,
  input  en_remainder,
  input  [1:0] sel_remainder,
  input  [3:0] divisor_in,
  input  en_divisor,
  input  sel_divisor,
  output [7:0] quotient_out,
  output i_ge_zero,
  output remainder_lt_zero
);

  wire comparator_1_gt, comparator_2_eq;
  wire [7:0] adder_1_out, divisor_q, i_q, multiplexer_1_out, multiplexer_2_out, multiplexer_3_out,
       multiplexer_4_out, remainder_q, shifter_1_out, subtractor_1_out, subtractor_2_out;

  Subtractor subtractor_1 (.a(remainder_q), .b(divisor_q), .out(subtractor_1_out));  // open: bin, bout
  Adder adder_1 (.a(remainder_q), .b(divisor_q), .out(adder_1_out));  // open: cin, cout
  Shifter #(.shift("lr")) shifter_1 (.in(divisor_q), .\dist (3'b001), .out(shifter_1_out));
  Subtractor subtractor_2 (.a(i_q), .b(8'h1), .out(subtractor_2_out));  // open: bin, bout
  Multiplexer #(.select(2), .width(8)) multiplexer_1 (
    .in0({8{1'b0}}), .in1({quotient_out[6:0], 1'b0}), .in2({quotient_out[6:0], 1'b1}),
    .out(multiplexer_1_out), .sel(sel_quotient));  // open: in3
  Multiplexer #(.width(8)) multiplexer_2 (.in0(8'h4), .in1(subtractor_2_out), .out(multiplexer_2_out), .sel(sel_i));
  Multiplexer #(.select(2), .width(8)) multiplexer_3 (
    .in0({4'b0000, dividend_in}), .in1(subtractor_1_out), .in2(adder_1_out), .out(multiplexer_3_out),
    .sel(sel_remainder));  // open: in3
  Multiplexer #(.width(8)) multiplexer_4 (
    .in0({divisor_in, 4'b0000}), .in1(shifter_1_out), .out(multiplexer_4_out), .sel(sel_divisor));
  load_register8 quotient (.d(multiplexer_1_out), .en(en_quotient), .clk(clk), .q(quotient_out));  // open: rst
  load_register8 i (.d(multiplexer_2_out), .en(en_i), .clk(clk), .q(i_q));  // open: rst
  load_register8 remainder (.d(multiplexer_3_out), .en(en_remainder), .clk(clk), .q(remainder_q));  // open: rst
  load_register8 divisor (.d(multiplexer_4_out), .en(en_divisor), .clk(clk), .q(divisor_q));  // open: rst
  Comparator comparator_1 (.a(multiplexer_2_out), .b({8{1'b0}}), .gt(comparator_1_gt));  // open: eq, lt
  Comparator comparator_2 (.a(multiplexer_2_out), .b({8{1'b0}}), .eq(comparator_2_eq));  // open: gt, lt
  Comparator comparator_3 (.a(multiplexer_3_out), .b({8{1'b0}}), .lt(remainder_lt_zero));  // open: gt, eq
  or or_1 (i_ge_zero, comparator_1_gt, comparator_2_eq);
endmodule

module fsm_state_reg3 (
  input  [2:0] next_state,
  input  clk,
  output [2:0] state
);

  Register #(.width(3)) register_1 (.D(next_state), .en(1'b1), .clk(clk), .Q(state));  // open: clr
endmodule

module div_comb (
  input  [2:0] p,
  input  i_ge_zero,
  input  remainder_lt_zero,
  input  start,
  output [2:0] n,
  output en_quotient,
  output [1:0] sel_quotient,
  output en_i,
  output sel_i,
  output en_remainder,
  output [1:0] sel_remainder,
  output en_divisor,
  output sel_divisor
);

  wire and_1_out, and_2_out, and_3_out, and_4_out, and_5_out, and_6_out, and_7_out, and_8_out, and_9_out,
       and_10_out, and_11_out, and_12_out, and_17_out, and_18_out, not_1_out, not_2_out, not_3_out,
       not_4_out, not_5_out;

  not not_1 (not_1_out, p[2]);
  not not_2 (not_2_out, p[1]);
  not not_3 (not_3_out, p[0]);
  not not_4 (not_4_out, i_ge_zero);
  not not_5 (not_5_out, remainder_lt_zero);
  and and_1 (and_1_out, p[2], not_2_out, not_3_out);
  and and_2 (and_2_out, not_1_out, p[1], not_5_out);
  and and_3 (and_3_out, p[1], p[0]);
  and and_4 (and_4_out, p[2], not_2_out, not_4_out);
  and and_5 (and_5_out, not_2_out, p[0]);
  and and_6 (and_6_out, not_1_out, p[1], not_3_out, remainder_lt_zero);
  and and_7 (and_7_out, p[2], not_2_out, not_3_out);
  and and_8 (and_8_out, not_2_out, not_3_out, start);
  and and_9 (and_9_out, not_1_out, p[1], remainder_lt_zero);
  and and_10 (and_10_out, p[1], p[0]);
  and and_11 (and_11_out, p[2], not_2_out, not_3_out);
  and and_12 (and_12_out, not_1_out, p[0]);
  and and_13 (sel_quotient[1], p[2], not_2_out, not_3_out);
  and and_14 (sel_quotient[0], p[1], p[0]);
  and and_15 (en_i, not_2_out, p[0]);
  and and_16 (sel_i, p[2], p[0]);
  and and_17 (and_17_out, not_1_out, p[0]);
  and and_18 (and_18_out, not_1_out, p[1]);
  and and_19 (sel_remainder[1], p[1], p[0]);
  and and_20 (sel_remainder[0], not_1_out, p[1], not_3_out);
  and and_21 (en_divisor, not_2_out, p[0]);
  and and_22 (sel_divisor, p[2], p[0]);
  or or_1 (n[2], and_1_out, and_2_out, and_3_out, and_4_out);
  or or_2 (n[1], and_5_out, and_6_out);
  or or_3 (n[0], and_7_out, and_8_out, and_9_out, and_10_out);
  or or_4 (en_quotient, and_11_out, and_12_out);
  or or_5 (en_remainder, and_17_out, and_18_out);
endmodule

module div_controller (
  input  clk,
  input  i_ge_zero,
  input  remainder_lt_zero,
  input  start,
  output en_quotient,
  output [1:0] sel_quotient,
  output en_i,
  output sel_i,
  output en_remainder,
  output [1:0] sel_remainder,
  output en_divisor,
  output sel_divisor
);

  wire [2:0] div_comb_1_n, fsm_state_reg3_1_state;

  fsm_state_reg3 fsm_state_reg3_1 (.next_state(div_comb_1_n), .clk(clk), .state(fsm_state_reg3_1_state));
  div_comb div_comb_1 (
    .p(fsm_state_reg3_1_state), .i_ge_zero(i_ge_zero), .remainder_lt_zero(remainder_lt_zero), .start(start),
    .n(div_comb_1_n), .en_quotient(en_quotient), .sel_quotient(sel_quotient), .en_i(en_i), .sel_i(sel_i),
    .en_remainder(en_remainder), .sel_remainder(sel_remainder), .en_divisor(en_divisor),
    .sel_divisor(sel_divisor));
endmodule

module div_processor (
  input  [3:0] dividend_in,
  input  [3:0] divisor_in,
  input  clk,
  input  start,
  output [7:0] quotient_out
);

  wire div_controller_1_en_divisor, div_controller_1_en_i, div_controller_1_en_quotient,
       div_controller_1_en_remainder, div_controller_1_sel_divisor, div_controller_1_sel_i,
       div_datapath_1_i_ge_zero, div_datapath_1_remainder_lt_zero;
  wire [1:0] div_controller_1_sel_quotient, div_controller_1_sel_remainder;

  div_controller div_controller_1 (
    .clk(clk), .i_ge_zero(div_datapath_1_i_ge_zero), .remainder_lt_zero(div_datapath_1_remainder_lt_zero),
    .start(start), .en_quotient(div_controller_1_en_quotient), .sel_quotient(div_controller_1_sel_quotient),
    .en_i(div_controller_1_en_i), .sel_i(div_controller_1_sel_i),
    .en_remainder(div_controller_1_en_remainder), .sel_remainder(div_controller_1_sel_remainder),
    .en_divisor(div_controller_1_en_divisor), .sel_divisor(div_controller_1_sel_divisor));
  div_datapath div_datapath_1 (
    .clk(clk), .en_quotient(div_controller_1_en_quotient), .sel_quotient(div_controller_1_sel_quotient),
    .en_i(div_controller_1_en_i), .sel_i(div_controller_1_sel_i), .dividend_in(dividend_in),
    .en_remainder(div_controller_1_en_remainder), .sel_remainder(div_controller_1_sel_remainder),
    .divisor_in(divisor_in), .en_divisor(div_controller_1_en_divisor),
    .sel_divisor(div_controller_1_sel_divisor), .quotient_out(quotient_out),
    .i_ge_zero(div_datapath_1_i_ge_zero), .remainder_lt_zero(div_datapath_1_remainder_lt_zero));
endmodule
